# Fritzing sketch dcmotor (saved by Fritzing 0.9.2b)
breadboards: 1

parts:
  Part1 = 16-Channel 12-bit PCA9685 PWM/Servo Driver
  M1 = DC Motor
  R1 = Resistor [tolerance=±5% resistance=330 package=THT]  # not connected
  Q1 = PNP-Transistor [package="TO92 [THT]"]
  D1 = Rectifier Diode [part_number=1N4007 package="300 mil [THT]"]
  Power_plug1 = Power plug
  Raspberry_Pi1 = Raspberry Pi 2

nets:
  N1: Part1.PWRIN, Power_plug1.VCC
  GND: Part1.GND, Q1.E, Power_plug1.GND, Raspberry_Pi1.GND
  N2: Part1.V+, M1.pin_2, D1.cathode
  VCC: Part1.VCC, Raspberry_Pi1.5V
  N3: Part1.SDA, Raspberry_Pi1.ID_SC
  N4: Part1.SCL, Raspberry_Pi1.ID_SD
  N5: M1.pin_1, Q1.C, D1.anode

custom parts:
  16-Channel 12-bit PCA9685 PWM/Servo Driver: The Adafruit 16-Channel 12-bit PWM/Servo Driver will drive up to 16 servos over I2C with only 2 pins. The on-board PCA9685 PWM controller will drive all 16 channels simultaneously with no additional processing overhead. What's more, you can chain up to 62 of them to control up to 992 servos - all with the same 2 pins
